# Fritzing sketch Flappy_1d (saved by Fritzing 1.0.2b)
breadboards: 1

parts:
  part = Raspberry Pi Pico
  Knob_Controller = POT [knob_status=50% power=0.5W package=pot_mammoth]
  Dotstar_strip = Camdenboss CTB0158-4 [part_number=CTB0158-4 package=THT]
  5v_Power_supply = DC Power [voltage=5]

nets:
  N1: part.pin_3, part.pin_13, part.pin_23, part.pin_38, part.pin_42, Knob_Controller.E, Dotstar_strip.pin2, 5v_Power_supply.V-
  N2: part.pin_4, Dotstar_strip.pin3
  N3: part.pin_5, Dotstar_strip.pin4
  N4: part.pin_31, Knob_Controller.S
  N5: part.pin_36, Knob_Controller.A
  N6: part.pin_40, Dotstar_strip.pin1, 5v_Power_supply.V+

notes:
  Red 5v
  Black Gnd
  Yellow? Clock
  Green? Data

custom parts:
  Raspberry Pi Pico: Raspberry Pi Pico. Based around the RP2040 microcontroller the Pico is a low cost microcontroller device bringing Raspberry Pi quality, cost, and easy of use to the microcontroller space. Jan 2021, Split part in to two versions: SMD (this one) and tht. This one is single sided and uses the castellation pads to solder the module to the board (no holes, other than for the USB connector!). The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
